# Fritzing sketch controlFAN (saved by Fritzing 1.0.4)
circuit board: 3cm x 3cm
breadboards: 1

parts:
  C2 = Electrolytic Capacitor [capacitance=100µF voltage=35V package="200 mil [THT, electrolytic]"]
  C1 = Ceramic Capacitor [capacitance=0.1µF voltage=16V package="100 mil [THT, multilayer]"]
  J1 = female pin header, 2 pins [form="♀ (female)"]
  R3 = Rotary Potentiometer (Large) [maximum_resistance=5kΩ knob_status=50% power=0.5W package=THT]
  R1 = Resistor [tolerance=±5% resistance=100 package=THT]
  R2 = Resistor [tolerance=±5% resistance=100k package=THT]
  Q7 = Basic FET N-Channel [package="TO220 [THT]"]
  + = female pin header, 1 pin [form="♀ (female)"]
  - = female pin header, 1 pin [form="♀ (female)"]

nets:
  N1: C2.-, R3.leg2, R2.Pin_1, Q7.source, -.pin1
  N2: C2.+, C1.0, J1.pin1, R3.leg1, +.pin1
  N3: C1.1, J1.pin2, Q7.drain
  N4: R3.wiper, R1.Pin_1
  N5: R1.Pin_0, R2.Pin_0, Q7.gate
